// Logisim project PacMo.circ as structural Verilog: 1 circuit, main circuit main
module main (
  input  [1:0] ReadReg1,
  input  [1:0] WriteReg,
  input  RegWrite,
  input  [7:0] RegDataW,
  input  [1:0] ReadReg2,
  input  [1:0] OpCode,
  output [7:0] RegData1,
  output [7:0] RegData2
);

  wire and_1_out, and_2_out, and_3_out, and_4_out, Clock1_out, decoder_1_out0, decoder_1_out1,
       decoder_1_out2, decoder_1_out3, decoder_2_out0, decoder_2_out1, decoder_2_out2, decoder_2_out3,
       undriven;
  wire [7:0] adder_1_out, adder_2_out, multiplexer_3_out, PC_q, subtractor_1_out, X1_q, X2_q, X3_q, X4_q;

  Clock Clock1 (.out(Clock1_out));
  Register PC (.D(adder_1_out), .clk(Clock1_out), .Q(PC_q));  // open: en, clr
  Adder adder_1 (.a(PC_q), .b(8'h1), .out(adder_1_out));  // open: cin, cout
  Decoder #(.select(2)) decoder_1 (
    .out0(decoder_1_out0), .out1(decoder_1_out1), .out2(decoder_1_out2), .out3(decoder_1_out3), .sel(OpCode));  // open: en
  Decoder #(.select(2)) decoder_2 (
    .out0(decoder_2_out0), .out1(decoder_2_out1), .out2(decoder_2_out2), .out3(decoder_2_out3), .sel(WriteReg));  // open: en
  Register X1 (.D(RegDataW), .en(and_1_out), .clk(Clock1_out), .Q(X1_q));  // open: clr
  and and_1 (and_1_out, RegWrite, decoder_2_out0);
  Register X2 (.D(RegDataW), .en(and_2_out), .clk(Clock1_out), .Q(X2_q));  // open: clr
  and and_2 (and_2_out, RegWrite, decoder_2_out1);
  Register X3 (.D(RegDataW), .en(and_3_out), .clk(Clock1_out), .Q(X3_q));  // open: clr
  and and_3 (and_3_out, RegWrite, decoder_2_out2);
  Register X4 (.D(RegDataW), .en(and_4_out), .clk(Clock1_out), .Q(X4_q));  // open: clr
  and and_4 (and_4_out, RegWrite, decoder_2_out3);
  Multiplexer #(.select(2), .width(8)) multiplexer_1 (
    .in0(X1_q), .in1(X2_q), .in2(X3_q), .in3(X4_q), .out(RegData1), .sel(ReadReg1));
  Multiplexer #(.select(2), .width(8)) multiplexer_2 (
    .in0(X1_q), .in1(X2_q), .in2(X3_q), .in3(X4_q), .out(RegData2), .sel(ReadReg2));
  Adder adder_2 (.a(RegData1), .b(RegData2), .out(adder_2_out));  // open: cin, cout
  Subtractor subtractor_1 (.a(RegData1), .b(RegData2), .out(subtractor_1_out));  // open: bin, bout
  Multiplexer #(.width(8)) multiplexer_3 (
    .in0(adder_2_out), .in1(subtractor_1_out), .out(multiplexer_3_out), .sel(undriven));
  RAM ram_1 (.addr(multiplexer_3_out), .clk(Clock1_out), .din(RegData2));  // open: we, oe, dout

  // Notes on the sheet:
  //   Jake Paccione & Matthew Mohamed | Lab 8
  //   Write Port
  //   Read Port 1
  //   Read Port 2
endmodule
